# Fritzing sketch Wiring (saved by Fritzing 0.9.3b)

parts:
  Raspberry_Pi_1 = Raspberry Pi 3 [part_number=RPI-3-V1.2]  # not connected
  Part1 = Adafruit DC+Stepper Motor HAT [part_number="Adafruit #2348"]
  M1 = DC Motor
  M2 = DC Motor
  M3 = DC Motor
  M4 = DC Motor
  LED1 = LED - 5mm [color="Red (633nm)" package="5 mm [THT]"]

nets:
  N1: Part1.M2A, M4.pin_1
  N2: Part1.M2B, M4.pin_2
  N3: Part1.M1B, M3.pin_1
  N4: Part1.M1A, M3.pin_2
  N5: Part1.M4A, M1.pin_1
  N6: Part1.M4B, M1.pin_2
  N7: Part1.M3B, M2.pin_1
  N8: Part1.M3A, M2.pin_2
  N9: Part1.PWM0, LED1.anode
  N10: Part1.GND, LED1.cathode

custom parts:
  Adafruit DC+Stepper Motor HAT: Let your robotic dreams come true with the new DC+Stepper Motor HAT from Adafruit. This Raspberry Pi add-on is perfect for any motion project as it can drive up to 4 DC or 2 Stepper motors with full PWM speed control. Since the Raspberry Pi does not have a lot of PWM pins, we use a fully-dedicated PWM driver chip onboard to both control motor direction and speed. This chip handles all the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
